# Fritzing sketch VL6180_MUX_Controller (saved by Fritzing 0.9.2b)
circuit board: 9.02cm x 3.02cm
breadboards: 1

parts:
  S4 = Generic male header - 7 pins [form="♂ (male)" package=THT]
  S3 = Generic male header - 7 pins [form="♂ (male)" package=THT]
  S2 = Generic male header - 7 pins [form="♂ (male)" package=THT]
  S1 = Generic male header - 7 pins [form="♂ (male)" package=THT]
  S0 = Generic male header - 7 pins [form="♂ (male)" package=THT]
  MUX = DIP - 16 pins [chip_label=CD4501B package="DIP (Dual Inline) [THT]"]
  INPUT = Generic male header - 7 pins [form="♂ (male)" package=THT]

nets:
  N1: S4.SCL, S3.SCL, S2.SCL, S1.SCL, S0.SCL, INPUT.SCL
  N2: S4.SDA, MUX.4
  GND: S4.GND, S3.GND, S2.GND, S1.GND, S0.GND, MUX.INH, MUX.VEE, MUX.VSS, INPUT.GND
  VDD: S4.VDD, S3.VDD, S2.VDD, S1.VDD, S0.VDD, MUX.VDD, INPUT.VDD
  N3: S3.SDA, MUX.3
  N4: S2.SDA, MUX.2
  N5: S1.SDA, MUX.1
  N6: S0.SDA, MUX.0
  N7: MUX.COM_IN/OUT, INPUT.SDA
  N8: MUX.C, INPUT.C
  N9: MUX.B, INPUT.B
  N10: MUX.A, INPUT.A

notes:
  SCL
  SDA
  A
  B
  C
  VDD
  GND
  Multi VL6180 v1.0

custom parts:
  Generic male header - 7 pins: Generic male header
  DIP - 16 pins: A DIP stand-in part for whatever IC you want. With 16 pins on a 300mil dual inline package (DIP) footprint.
  Generic male header - 7 pins: Generic male header
